# Fritzing sketch RGB-binary-clock-MB-fritzing (saved by Fritzing 0.9.3b)
breadboards: 1

parts:
  Súčiastka1 = Arduino Nano (Rev3.0) (ICSP)
  R15 = Resistor Mini [tolerance=±1% resistance=330 package=THT]
  R16 = Resistor Mini [tolerance=±1% resistance=360 package=THT]
  R17 = Resistor Mini [tolerance=±1% resistance=360 package=THT]
  R18 = Resistor Mini [tolerance=±1% resistance=330 package=THT]
  LED1 = RGB LED (com. cathode, rgb) [package="5 mm [THT]"]
  LED2 = RGB LED (com. cathode, rgb) [package="5 mm [THT]"]
  LED3 = RGB LED (com. cathode, rgb) [package="5 mm [THT]"]
  LED4 = RGB LED (com. cathode, rgb) [package="5 mm [THT]"]
  LED5 = RGB LED (com. cathode, rgb) [package="5 mm [THT]"]
  LED6 = RGB LED (com. cathode, rgb) [package="5 mm [THT]"]
  S1 = Toggle Switch [package=THT]
  R19 = Resistor Mini [tolerance=±1% resistance=330 package=THT]
  R20 = Resistor Mini [tolerance=±1% resistance=330 package=THT]
  R21 = Resistor Mini [tolerance=±1% resistance=330 package=THT]
  R22 = Resistor Mini [tolerance=±1% resistance=330 package=THT]
  R23 = Resistor Mini [tolerance=±1% resistance=330 package=THT]
  R24 = Resistor Mini [tolerance=±1% resistance=330 package=THT]
  R25 = Resistor Mini [tolerance=±1% resistance=330 package=THT]
  R26 = Resistor Mini [tolerance=±1% resistance=330 package=THT]
  R27 = Resistor Mini [tolerance=±1% resistance=360 package=THT]
  R28 = Resistor Mini [tolerance=±1% resistance=360 package=THT]
  R29 = Resistor Mini [tolerance=±1% resistance=360 package=THT]
  R30 = Resistor Mini [tolerance=±1% resistance=360 package=THT]

nets:
  N1: Súčiastka1.GND, LED1.common_cathode, LED2.common_cathode, LED3.common_cathode, LED4.common_cathode, LED5.common_cathode, LED6.common_cathode
  N2: Súčiastka1.D2, R26.Pin_0
  N3: Súčiastka1.D3, R24.Pin_0
  N4: Súčiastka1.D4, R22.Pin_0
  N5: Súčiastka1.D5, R15.Pin_0
  N6: Súčiastka1.D6, R25.Pin_0
  N7: Súčiastka1.D7, R23.Pin_0
  N8: Súčiastka1.D8, R21.Pin_0
  N9: Súčiastka1.D9, R19.Pin_0
  N10: Súčiastka1.D10, R18.Pin_0
  N11: Súčiastka1.D11/MOSI, R27.Pin_1
  N12: Súčiastka1.D12/MISO, R28.Pin_0
  N13: Súčiastka1.5V, S1.L2
  N14: Súčiastka1.A5, R20.Pin_0
  N15: Súčiastka1.A3, S1.COM
  N16: Súčiastka1.A2, R29.Pin_0
  N17: Súčiastka1.A1, R30.Pin_1
  N18: Súčiastka1.A0, R17.Pin_0
  N19: Súčiastka1.D13/SCK, R16.Pin_1

custom parts:
  Resistor Mini: A generic resistor (0.25W)
